# Fritzing sketch Rangkaian IoT (saved by Fritzing 0.9.3b)
breadboards: 1

parts:
  Part1 = Arduino Nano (Rev3.0)
  Part2 = Bluetooth HC-05 Macho
  LED1 = LED - 3mm [color="Red (633nm)" package="3 mm [THT]"]
  R1 = Resistor [tolerance=±5% resistance=220 package="1206 [SMD]"]
  Part3 = Real Time Clock Module - DS1307 RTC Breakout Board

nets:
  GND: Part1.GND, Part2.GND, R1.Pin_0, Part3.GND
  N1: Part1.D2, Part2.TXD
  N2: Part1.D3, Part2.RXD
  5V: Part1.5V, Part2.VCC, Part3.5V
  N3: Part1.A5, Part3.SCL
  N4: Part1.A4, Part3.SDA
  N5: Part1.D13/SCK, LED1.anode
  N6: LED1.cathode, R1.Pin_1
